# Fritzing sketch juke (saved by Fritzing 0.9.2b)
circuit board: 13.4cm x 20.3cm
breadboards: 2

parts:
  J1 = female pin header, 20 pins [form="♀ (female)"]
  Q1 = TRANSISTOR_NPN [package=to-92]
  Q2 = TRANSISTOR_NPN [package=to-92]
  Q3 = TRANSISTOR_NPN [package=to-92]
  Q4 = TRANSISTOR_NPN [package=to-92]
  R1 = Resistor [tolerance=±5% resistance=1k power=0pW package=THT]
  R2 = Resistor [tolerance=±5% resistance=1k power=0pW package=THT]
  R4 = Resistor [tolerance=±5% resistance=1k power=0pW package=THT]
  R8 = Resistor [tolerance=±5% resistance=1k power=0pW package=THT]
  R9 = Resistor [tolerance=±5% resistance=100k package=THT]
  R10 = Resistor [tolerance=±5% resistance=100k package=THT]
  R11 = Resistor [tolerance=±5% resistance=100k package=THT]
  R13 = Resistor [tolerance=±5% resistance=51k package=THT]
  R14 = Resistor [tolerance=±5% resistance=51k package=THT]
  R15 = Resistor [tolerance=±5% resistance=51k package=THT]
  Q5 = TRANSISTOR_NPN [package=to-92]
  Q6 = TRANSISTOR_NPN [package=to-92]
  Q7 = TRANSISTOR_NPN [package=to-92]
  Q8 = TRANSISTOR_NPN [package=to-92]
  R17 = Resistor [tolerance=±5% resistance=1k power=0pW package=THT]
  R19 = Resistor [tolerance=±5% resistance=1k power=0pW package=THT]
  R20 = Resistor [tolerance=±5% resistance=1k power=0pW package=THT]
  J3 = male pin header, 4 pins [form="♂ (male)"]
  C1 = Electrolytic Capacitor [capacitance=10µF package="100 mil [THT, electrolytic]"]
  J2 = female pin header, 10 pins [form="♀ (female)"]
  J5 = female pin header, 9 pins [form="♀ (female)"]
  C2 = Electrolytic Capacitor [capacitance=10µF package="100 mil [THT, electrolytic]"]
  U2 = RJ45 Jack [package=rj45-8]
  R3 = Resistor [tolerance=±20% resistance=10k package=THT]
  R5 = Resistor [tolerance=±20% resistance=10k package=THT]
  R7 = Resistor [tolerance=±20% resistance=10k package=THT]
  R21 = Resistor [tolerance=±5% resistance=1k power=0pW package=THT]
  R6 = Resistor [tolerance=±20% resistance=10k package=THT]
  J12 = male pin header, 1 pin [form="♂ (male)"]  # not connected
  J13 = male pin header, 1 pin [form="♂ (male)"]  # not connected
  J14 = male pin header, 1 pin [form="♂ (male)"]  # not connected
  J15 = male pin header, 1 pin [form="♂ (male)"]  # not connected
  J16 = male pin header, 1 pin [form="♂ (male)"]  # not connected
  J17 = male pin header, 1 pin [form="♂ (male)"]  # not connected
  J18 = male pin header, 1 pin [form="♂ (male)"]  # not connected
  J19 = male pin header, 1 pin [form="♂ (male)"]  # not connected
  J20 = male pin header, 1 pin [form="♂ (male)"]  # not connected
  J21 = male pin header, 1 pin [form="♂ (male)"]  # not connected
  J22 = male pin header, 1 pin [form="♂ (male)"]  # not connected
  J23 = male pin header, 1 pin [form="♂ (male)"]  # not connected
  J24 = male pin header, 1 pin [form="♂ (male)"]  # not connected
  U1 = Voltage Regulator [package=to220-igo]
  J38 = male pin header, 1 pin [form="♂ (male)"]  # not connected
  J35 = male pin header, 1 pin [form="♂ (male)"]
  J37 = male pin header, 1 pin [form="♂ (male)"]
  J40 = male pin header, 1 pin [form="♂ (male)"]  # not connected
  J39 = male pin header, 1 pin [form="♂ (male)"]  # not connected
  J33 = male pin header, 1 pin [form="♂ (male)"]  # not connected
  J34 = male pin header, 1 pin [form="♂ (male)"]
  J36 = male pin header, 1 pin [form="♂ (male)"]
  J45 = male pin header, 1 pin [form="♂ (male)"]
  J46 = male pin header, 1 pin [form="♂ (male)"]  # not connected
  J44 = male pin header, 1 pin [form="♂ (male)"]
  J48 = male pin header, 1 pin [form="♂ (male)"]  # not connected
  J41 = male pin header, 1 pin [form="♂ (male)"]
  J47 = male pin header, 1 pin [form="♂ (male)"]
  J49 = male pin header, 1 pin [form="♂ (male)"]
  J50 = male pin header, 1 pin [form="♂ (male)"]
  J51 = male pin header, 1 pin [form="♂ (male)"]
  J52 = male pin header, 1 pin [form="♂ (male)"]
  J53 = male pin header, 1 pin [form="♂ (male)"]
  J54 = male pin header, 1 pin [form="♂ (male)"]
  J55 = male pin header, 1 pin [form="♂ (male)"]  # not connected
  J56 = male pin header, 1 pin [form="♂ (male)"]
  J57 = male pin header, 1 pin [form="♂ (male)"]
  J58 = male pin header, 1 pin [form="♂ (male)"]
  J59 = male pin header, 1 pin [form="♂ (male)"]  # not connected
  J60 = male pin header, 1 pin [form="♂ (male)"]  # not connected
  J61 = male pin header, 1 pin [form="♂ (male)"]
  J62 = male pin header, 1 pin [form="♂ (male)"]
  J63 = male pin header, 1 pin [form="♂ (male)"]
  J64 = male pin header, 1 pin [form="♂ (male)"]  # not connected
  J65 = male pin header, 1 pin [form="♂ (male)"]
  J66 = male pin header, 1 pin [form="♂ (male)"]  # not connected
  J67 = male pin header, 1 pin [form="♂ (male)"]  # not connected
  J68 = male pin header, 1 pin [form="♂ (male)"]  # not connected
  J69 = male pin header, 1 pin [form="♂ (male)"]  # not connected
  J70 = male pin header, 1 pin [form="♂ (male)"]  # not connected
  J71 = male pin header, 1 pin [form="♂ (male)"]  # not connected
  J72 = male pin header, 1 pin [form="♂ (male)"]  # not connected
  J73 = male pin header, 1 pin [form="♂ (male)"]
  J74 = male pin header, 1 pin [form="♂ (male)"]  # not connected
  J75 = male pin header, 1 pin [form="♂ (male)"]  # not connected
  J76 = male pin header, 1 pin [form="♂ (male)"]  # not connected
  J77 = male pin header, 1 pin [form="♂ (male)"]  # not connected
  J78 = male pin header, 1 pin [form="♂ (male)"]
  J79 = male pin header, 1 pin [form="♂ (male)"]  # not connected
  J80 = male pin header, 1 pin [form="♂ (male)"]
  J81 = male pin header, 1 pin [form="♂ (male)"]
  J82 = male pin header, 1 pin [form="♂ (male)"]  # not connected
  J83 = male pin header, 1 pin [form="♂ (male)"]  # not connected
  J84 = male pin header, 1 pin [form="♂ (male)"]  # not connected
  J85 = male pin header, 1 pin [form="♂ (male)"]
  J86 = male pin header, 1 pin [form="♂ (male)"]

nets (from the pcb view):
  N1: J1.pin2, J56.pin1
  N2: J1.pin4, J54.pin1
  N3: J1.pin5, J81.pin1
  N4: J1.pin6, J80.pin1
  N5: J1.pin9, J1.pin11, J85.pin1, J86.pin1
  N6: J1.pin13, R19.Pin_0
  N7: J1.pin14, R11.Pin_0, R15.Pin_1
  N8: J1.pin15, R10.Pin_0, R14.Pin_1
  N9: J1.pin17, R9.Pin_0, R13.Pin_1
  N10: J1.pin18, J45.pin1, J44.pin1
  N11: J1.pin19, J41.pin1, J47.pin1
  N12: J1.pin20, Q1.E, Q2.E, Q3.E, Q4.E, R13.Pin_0, R14.Pin_0, R15.Pin_0, Q5.E, Q6.E, Q7.E, Q8.E, J3.pin1, C1.-, C2.-, R3.Pin_0, R7.Pin_0, U1.GND, J37.pin1, J36.pin1, J62.pin1, J65.pin1, J78.pin1
  N13: Q1.B, R1.Pin_1
  N14: Q1.C, R2.Pin_1, R3.Pin_1
  N15: Q2.B, R2.Pin_0
  N16: Q2.C, U2.3, R5.Pin_0
  N17: Q3.B, R4.Pin_1
  N18: Q3.C, R8.Pin_1, R7.Pin_1
  N19: Q4.B, R8.Pin_0
  N20: Q4.C, U2.6, R6.Pin_0
  N21: R1.Pin_0, J5.pin1
  N22: R4.Pin_0, J2.pin10
  N23: R9.Pin_1, U2.5
  N24: R10.Pin_1, U2.7
  N25: R11.Pin_1, U2.8
  N26: Q5.B, R20.Pin_1
  N27: Q5.C, J63.pin1
  N28: Q6.B, R19.Pin_1
  N29: Q6.C, J58.pin1
  N30: Q7.B, R21.Pin_1
  N31: Q7.C, J61.pin1
  N32: Q8.B, R17.Pin_1
  N33: Q8.C, J57.pin1
  N34: R17.Pin_0, J5.pin6
  N35: R20.Pin_0, J5.pin4
  N36: J3.pin4, C1.+, U1.OUT
  N37: J2.pin1, J50.pin1
  N38: J2.pin2, J52.pin1
  N39: J2.pin3, J53.pin1
  N40: J2.pin5, J51.pin1
  N41: J2.pin8, J49.pin1
  N42: J5.pin5, R21.Pin_0
  N43: J5.pin7, J35.pin1, J34.pin1
  N44: C2.+, R5.Pin_1, R6.Pin_1, U1.IN, J73.pin1
